# Fritzing sketch stac_gyro (saved by Fritzing 0.9.3b)

parts:
  Adafruit_Atmega32u1 = Adafruit Atmega32u4 Breakout Board [part_number="Atmega 32u4"]
  GY3 = MPU9250 JK EMC [form="♀ (female)" package=THT]

nets:
  N1: Adafruit_Atmega32u1.F4, GY3.pin4
  N2: Adafruit_Atmega32u1.F5, GY3.pin3
  N3: Adafruit_Atmega32u1.GND, GY3.pin2
  N4: Adafruit_Atmega32u1.3V, GY3.pin1

custom parts:
  MPU9250 JK EMC: Placa GY-9250 basada en conjunto de acelerómetro+giroscopios MPU-9250
